# Fritzing sketch questao2 (saved by Fritzing 0.9.3b)
breadboards: 2

parts:
  R2 = Rotary Potentiometer (Small) [maximum_resistance=100kΩ package=THT]
  U1 = NodeMCU V1.0

nets:
  N1: R2.wiper, U1.3V3

custom parts:
  NodeMCU V1.0: ESP8266 based NodeMCU

// code stored in the sketch: ex2.ino
void setup(){
	Serial.begin(9600);
}
void loop(){
	int potencia = analogRead(15);
	Serial.println(potencia);
	Serial.println(potencia*5/1024);
}
