# Fritzing sketch questao3 (saved by Fritzing 0.9.3b)
breadboards: 2

parts:
  LED4 = LED - 5mm [color="Red (633nm)" package="5 mm [THT]"]
  U2 = NodeMCU V1.0
  R3 = Rotary Potentiometer (Small) [maximum_resistance=100kΩ package=THT]

nets:
  N1: LED4.cathode, R3.leg1
  N2: LED4.anode, U2.D0
  N3: U2.A0, R3.wiper

custom parts:
  NodeMCU V1.0: ESP8266 based NodeMCU

// code stored in the sketch: ex3.ino
void setup(){
	Serial.begin(9600);
}
void loop(){
	int potencia = analogRead(A0);
	Serial.println(potencia);
	Serial.println(potencia*5/1024);
	analogWrite(D0,potencia);
}
