# Fritzing sketch pratica_3-1b (saved by Fritzing 0.9.3b)
breadboards: 1

parts:
  U1 = ESP8266 NodeMCU LoLin module
  J1 = Basic Servo
  R1 = Rotary Potentiometer (Small) [maximum_resistance=100kΩ package=THT]

nets:
  N1: U1.D2, J1.pulse
  VIN: U1.Vin, J1.vcc, R1.leg1
  GND: U1.GND, J1.gnd, R1.leg2
  N2: U1.A0, R1.wiper

custom parts:
  ESP8266 NodeMCU LoLin module: ESP8266 based NodeMCU
