# Fritzing sketch pratica_3-1c (saved by Fritzing 0.9.3b)
breadboards: 1

parts:
  R1 = Rotary Potentiometer (Small) [maximum_resistance=100kΩ package=THT]
  U1 = ESP8266 NodeMCU LoLin module
  J1 = Basic Servo
  Display_4x7 = Grove 4 Digit Display

nets:
  VCC: R1.leg1, U1.Vin, J1.vcc, Display_4x7.VCC
  N1: R1.wiper, U1.A0
  GND: R1.leg2, U1.GND, J1.gnd, Display_4x7.GND
  N2: U1.D2, J1.pulse
  N3: U1.D6, Display_4x7.CLK
  N4: U1.D7, Display_4x7.DIO

custom parts:
  ESP8266 NodeMCU LoLin module: ESP8266 based NodeMCU
