# Fritzing sketch pratica4tarefa1 (saved by Fritzing 0.9.3b)
breadboards: 1

parts:
  U1 = ESP8266 NodeMCU LoLin module
  R1 = PHOTOCELL [package=photocell-kit]
  R2 = PHOTOCELL [package=photocell-kit]
  T1 = LM35 Temperature Sensor [package="TO92 [THT]"]
  R3 = Resistor [tolerance=±5% resistance=220 package=THT]
  R4 = Resistor [tolerance=±5% resistance=220 package=THT]
  Componente1 = Analog Digital MUX Breakout

nets:
  N1: U1.D0, Componente1.S0
  N2: U1.D1, Componente1.S1
  3V3: U1.3V3, R1.P$1, R2.P$1, T1.+Vs, Componente1.VCC
  GND: U1.GND, T1.GND, R3.Pin_1, R4.Pin_1, Componente1.GND, Componente1.S2, Componente1.S3
  N3: U1.A0, Componente1.SIG
  N4: R1.P$2, R4.Pin_0, Componente1.C0
  N5: R2.P$2, R3.Pin_0, Componente1.C1
  N6: T1.Vout, Componente1.C2

custom parts:
  ESP8266 NodeMCU LoLin module: ESP8266 based NodeMCU
