# Fritzing sketch aula_2-tarefa_2 (saved by Fritzing 0.9.3b)
breadboards: 1

parts:
  U1 = ESP8266 NodeMCU LoLin module
  S1 = Pushbutton [package="[THT]"]
  S2 = Pushbutton [package="[THT]"]
  R1 = Resistor [tolerance=±5% resistance=220 package=THT]
  R2 = Resistor [tolerance=±5% resistance=220 package=THT]
  7400 = IC, DIP package, 14 pins [chip_label=IC]

nets:
  N1: U1.D0, 7400.pin1
  N2: U1.GND, S1.Pin_3, S1.Pin_4, S2.Pin_3, S2.Pin_4, R1.Pin_1, R2.Pin_1, 7400.pin2, 7400.pin7, 7400.pin10
  N3: U1.3V3, R1.Pin_0, R2.Pin_0, 7400.pin14
  N4: 7400.pin3, 7400.pin9

custom parts:
  ESP8266 NodeMCU LoLin module: ESP8266 based NodeMCU
