# Fritzing sketch aula_2-tarefa_3 (saved by Fritzing 0.9.3b)
breadboards: 2

parts:
  U1 = ESP8266 NodeMCU LoLin module
  R1 = Photocell (LDR) [package=THT]
  R2 = Resistor [tolerance=±5% resistance=1.5k package=THT]
  LED1 = smd LED [color="Red (633nm)" package="0603 [SMD]"]
  R3 = Resistor [tolerance=±5% resistance=220 package=THT]

nets:
  N1: U1.D1, R3.Pin_0
  N2: U1.3V3, R2.Pin_1
  N3: U1.GND, R1.pin_1, LED1.cathode
  N4: U1.A0, R1.pin_0, R2.Pin_0
  N5: LED1.anode, R3.Pin_1

custom parts:
  ESP8266 NodeMCU LoLin module: ESP8266 based NodeMCU
